# Fritzing sketch ultrasonic-car (saved by Fritzing 0.9.2b)

parts:
  Bauteil1 = SRF05 Ultrasonic Rangefinder
  Bauteil2 = Arduino Uno (Rev3)

nets:
  VCC: Bauteil1.VCC, Bauteil2.5V
  N1: Bauteil1.Trig, Bauteil2.D12/MISO
  N2: Bauteil1.Echo, Bauteil2.D13/SCK
  GND: Bauteil1.GND, Bauteil2.GND
