# Fritzing sketch waterdetector (saved by Fritzing 0.9.2b)
breadboards: 1

parts:
  Q1 = PNP-Transistor [package="TO92 [THT]"]
  Q2 = NPN-Transistor [package="TO92 [THT]"]
  R1 = Trimmer Potentiometer [maximum_resistance=10kΩ package=THT]
  LED1 = LED - 5mm [color="Red (633nm)" package="5 mm [THT]"]
  R2 = Resistor [tolerance=±5% resistance=470k package=THT]
  R3 = Resistor [tolerance=±5% resistance=33k package=THT]

nets:
  N1: Q1.E, Q2.E, LED1.cathode
  N2: Q1.B, R3.Pin_0
  N3: Q1.C, Q2.B
  N4: Q2.C, R1.leg1
  N5: R1.wiper, R3.Pin_1
  N6: LED1.anode, R2.Pin_1
